# Fritzing sketch controller (saved by Fritzing 0.9.3b)
circuit board: 7cm x 3cm
breadboards: 1

parts:
  Part1 = Arduino Nano (Rev3.0)
  Part2 = Barometric Pressure Sensor - BMP180 Breakout (GY-68)
  J2 = female pin header, 4 pins [form="♀ (female)"]
  J3 = female pin header, 4 pins [form="♀ (female)"]
  J4 = female pin header, 4 pins [form="♀ (female)"]
  J5 = female pin header, 2 pins [form="♀ (female)"]
  J6 = female pin header, 15 pins [form="♀ (female)"]
  J8 = female pin header, 7 pins [form="♀ (female)"]
  Part3 = InvenSense MPU6050
  J9 = female pin header, 1 pin [form="♀ (female)"]
  J10 = female pin header, 1 pin [form="♀ (female)"]
  J12 = female pin header, 2 pins [form="♀ (female)"]
  J13 = female pin header, 1 pin [form="♀ (female)"]
  J15 = female pin header, 4 pins [form="♀ (female)"]
  J16 = female pin header, 1 pin [form="♀ (female)"]
  J17 = female pin header, 3 pins [form="♀ (female)"]
  J7 = female pin header, 13 pins [form="♀ (female)"]
  J18 = female pin header, 8 pins [form="♀ (female)"]
  J19 = female pin header, 2 pins [form="♀ (female)"]
  J20 = female pin header, 1 pin [form="♀ (female)"]
  J21 = female pin header, 1 pin [form="♀ (female)"]  # not connected
  J22 = female pin header, 4 pins [form="♀ (female)"]
  J23 = female pin header, 1 pin [form="♀ (female)"]
  J24 = female pin header, 1 pin [form="♀ (female)"]  # not connected

nets:
  N1: Part1.D1/TX, J6.pin1, J19.pin2
  N2: Part1.D0/RX, J6.pin2, J19.pin1
  N3: Part1.RESET, J6.pin3, J18.pin3
  GND: Part1.GND, Part2.GND, J2.pin2, J3.pin3, J4.pin2, J5.pin1, J6.pin4, Part3.GND, J12.pin1, J15.pin2, J17.pin2, J7.pin1, J7.pin2, J7.pin3, J7.pin4, J7.pin5, J7.pin6, J7.pin7, J7.pin8, J7.pin9, J7.pin10, J7.pin11, J7.pin12, J7.pin13, J18.pin2, J23.pin1
  N4: Part1.D2, J6.pin5
  N5: Part1.D3, J6.pin6
  N6: Part1.D4, J6.pin7
  N7: Part1.D5, J6.pin8
  N8: Part1.D6, J6.pin9
  N9: Part1.D7, J6.pin10
  N10: Part1.D8, J6.pin11
  N11: Part1.D9, J6.pin12
  N12: Part1.D10, J6.pin13
  N13: Part1.D11/MOSI, J6.pin14
  N14: Part1.D12/MISO, J6.pin15
  VCC: Part1.VIN, Part2.VCC, J2.pin1, J3.pin4, J4.pin1, J5.pin2, Part3.VCC, J12.pin2, J13.pin1, J15.pin1, J17.pin3, J18.pin1, J22.pin1
  N15: Part1.5V, J18.pin4
  N16: Part1.A7, J18.pin5
  N17: Part1.A6, J18.pin6
  N18: Part1.A5, Part2.SCL, J2.pin3, J3.pin2, J4.pin3, Part3.SCL, J15.pin3, J16.pin1, J17.pin1, J18.pin7, J22.pin3
  N19: Part1.A4, Part2.SDA, J2.pin4, J3.pin1, J4.pin4, Part3.SDA, J9.pin1, J10.pin1, J15.pin4, J18.pin8, J22.pin4
  N20: Part1.A3, J8.pin1
  N21: Part1.A2, J8.pin2
  N22: Part1.A1, J8.pin3
  N23: Part1.A0, J8.pin4, J20.pin1
  N24: Part1.AREF, J8.pin5
  N25: Part1.3V3, J8.pin6
  N26: Part1.D13/SCK, J8.pin7

notes:
  +
  -
  IMU
  COMP
  I2C
  r
  t
  A0
