# Fritzing sketch corrector (saved by Fritzing 0.9.3b)
circuit board: 7cm x 6cm

parts:
  R1 = Resistor [tolerance=±5% resistance=220 package=THT]
  R2 = Resistor [tolerance=±5% resistance=220 package=THT]
  J17 = female pin header, 4 pins [form="♀ (female)"]

nets:
  N1: R1.Pin_1, R2.Pin_0, J17.pin1, J17.pin2, J17.pin3

notes:
  +
  -
  2
